// Logisim project 4-Bit-ALU-logisim.circ as structural Verilog: 1 circuit, main circuit main
module main (
);

  wire adder_1_cout, adder_2_cout, adder_3_cout, adder_4_cout, d_ff_1_q, demultiplexer_1_out0,
       demultiplexer_1_out1, not_1_out, xor_1_out, xor_2_out, xor_3_out, xor_4_out, xor_5_out;
  wire [3:0] adder_1_out, and_1_out, and_5_out, and_6_out, multiplexer_1_out, not_2_out, or_1_out;

  Demultiplexer #(.enable("false")) demultiplexer_1 (
    .out0(demultiplexer_1_out0), .out1(demultiplexer_1_out1), .in(1'b0), .sel(1'b1));
  and and_1 (and_1_out[0], demultiplexer_1_out0, 1'b1, 1'b1);
  and and_2 (and_1_out[1], demultiplexer_1_out0, 1'b0, 1'b1);
  and and_3 (and_1_out[2], demultiplexer_1_out0, 1'b1, 1'b0);
  and and_4 (and_1_out[3], demultiplexer_1_out0, 1'b1, 1'b1);
  or or_1 (or_1_out[0], demultiplexer_1_out1, 1'b1, demultiplexer_1_out0);
  or or_2 (or_1_out[1], demultiplexer_1_out1, 1'b0, 1'b1);
  or or_3 (or_1_out[2], demultiplexer_1_out1, 1'b1, 1'b0);
  or or_4 (or_1_out[3], demultiplexer_1_out1, 1'b1, 1'b1);
  Multiplexer #(.width(4), .enable("false")) multiplexer_1 (
    .in0(and_1_out), .in1(or_1_out), .out(multiplexer_1_out), .sel(1'b1));
  assign and_5_out = multiplexer_1_out & 4'b0000;  // AND_Gate and_5, 4 bits wide
  xor xor_1 (xor_1_out, 1'b1, 1'b1);
  xor xor_2 (xor_2_out, 1'b1, 1'b1);
  xor xor_3 (xor_3_out, 1'b0, 1'b1);
  xor xor_4 (xor_4_out, 1'b1, 1'b1);
  not not_1 (not_1_out, 1'b0);
  Adder #(.width(1)) adder_1 (.a(1'b1), .b(xor_1_out), .out(adder_1_out[0]), .cin(d_ff_1_q), .cout(adder_1_cout));
  Adder #(.width(1)) adder_2 (.a(1'b0), .b(xor_2_out), .out(adder_1_out[1]), .cin(adder_1_cout), .cout(adder_2_cout));
  Adder #(.width(1)) adder_3 (.a(1'b1), .b(xor_3_out), .out(adder_1_out[2]), .cin(adder_2_cout), .cout(adder_3_cout));
  Adder #(.width(1)) adder_4 (.a(1'b1), .b(xor_4_out), .out(adder_1_out[3]), .cin(adder_3_cout), .cout(adder_4_cout));
  xor xor_5 (xor_5_out, adder_4_cout, adder_3_cout);
  assign not_2_out = ~4'b0000;  // NOT_Gate not_2, 4 bits wide
  D_Flip_Flop d_ff_1 (
    .clk(xor_5_out), .D(adder_1_out[3]), .Q(d_ff_1_q), .preset(adder_4_cout), .en(1'b1), .reset(not_1_out));  // open: Qn
  assign and_6_out = not_2_out & adder_1_out;  // AND_Gate and_6, 4 bits wide
  // Probe on and_5_out
  // Probe on and_6_out
  // Probe on d_ff_1_q
  // Probe on adder_4_cout
endmodule
